# Fritzing sketch CutOff (saved by Fritzing 0.9.2b)
perfboards: 1

parts:
  Mod1 = Digispark
  U6 = TLP621 [package=THT]
  JP8 = Header 2 [package=molex-1x2_lock]
  JP9 = Header 3 [package=molex-1x3_lock]
  JP10 = Header 4 [package=molex-1x4_lock]
  KF-1 = KF-301 Relay [package=THT]
  R2 = Resistor [tolerance=±5% resistance=1k package="2010 [SMD]"]
  J3 = rounded female pin header, 3 pins [form="♀ (female rounded)"]

nets:
  N1: Mod1.P0, JP8.2
  N2: Mod1.P1, KF-1.signal, J3.pin1
  N3: Mod1.P2, U6.Pin_4
  N4: U6.Pin_1, JP10.4
  N5: U6.Pin_2, R2.Pin_1
  N6: U6.Pin_3, JP9.2, KF-1.ground, J3.pin2
  N7: JP9.1, KF-1.power, J3.pin3
  N8: JP10.1, R2.Pin_0

custom parts:
  Digispark: The Digispark is an Attiny85 based microcontroller development board similar to the Arduino line, only cheaper, smaller, and a bit less powerful. With a whole host of shields to extend its functionality and the ability to use the familiar Arduino IDE the Digispark is a great way to jump into electronics, or perfect for when an Arduino is too big or too much. May 2019 modified to correct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
  KF-301 Relay: KF-301
